# Fritzing sketch Buzzer-Button (saved by Fritzing 0.9.6b)
breadboards: 1

parts:
  Part2 = Arduino Uno (Rev3) - ICSP
  Mod1 = Passive Buzzer
  S1 = Pushbutton [package="[THT]"]

nets:
  N1: Part2.GND, Mod1.-, S1.Pin_3, S1.Pin_4
  N2: Part2.D8, Mod1.S
  N3: Part2.D3_PWM, S1.Pin_1, S1.Pin_2
