# Fritzing sketch 3LED-PWM (saved by Fritzing 0.9.6b)
breadboards: 1

parts:
  Part1 = Arduino Uno (Rev3)
  LED1 = LED - 3mm [color="Red (633nm)" current=0.030 package="3 mm [THT]"]
  LED2 = LED - 3mm [color="Yellow (595nm)" current=0.030 package="3 mm [THT]"]
  LED3 = LED - 3mm [color="Blue (470nm)" current=0.030 package="3 mm [THT]"]

nets:
  N1: Part1.D9_PWM, LED1.anode
  N2: Part1.D10_PWM/SS, LED2.anode
  N3: Part1.D11_PWM/MOSI, LED3.anode
  N4: Part1.GND, LED1.cathode, LED2.cathode, LED3.cathode
