# Fritzing sketch PushLED (saved by Fritzing 0.9.6b)
breadboards: 1

parts:
  Part1 = Arduino Uno (Rev3)
  R1 = Resistor [tolerance=±5% power=0.25 resistance=220 package=THT]
  S1 = Momentary Switch [package=ksa_sealed_tac_switch]  # not connected
  LED1 = smd LED [color="Orange (605nm)" package="0805 [SMD]"]

nets:
  N1: Part1.GND, LED1.cathode
  N2: Part1.D3_PWM, R1.Pin_0
  N3: R1.Pin_1, LED1.anode
