# Fritzing sketch Arduino_Pong (saved by Fritzing 0.9.6b)
breadboards: 1

parts:
  OLED1 = OLED 128x64 I2C Monochrome Display
  Part1 = Arduino Uno (Rev3) - ICSP
  J1 = Piezo Speaker
  S1 = Pushbutton [package="[SMD]"]
  S2 = Pushbutton [package="[SMD]"]
  S3 = Pushbutton [package="[SMD]"]
  S4 = Pushbutton [package="[SMD]"]
  R1 = Resistor [tolerance=±5% resistance=10k package="2512 [SMD]"]
  R2 = Resistor [tolerance=±5% resistance=10k package="2512 [SMD]"]
  R3 = Resistor [tolerance=±5% resistance=10k package="2512 [SMD]"]
  R4 = Resistor [tolerance=±5% resistance=10k package="2512 [SMD]"]

nets:
  GND: OLED1.GND, Part1.GND, J1.pin1, R1.Pin_1, R2.Pin_1, R3.Pin_1, R4.Pin_1
  VDD: OLED1.VDD, Part1.5V
  N1: OLED1.SCK, Part1.A5/SCL
  N2: OLED1.SDA, Part1.A4/SDA
  N3: Part1.D9_PWM, S1.Pin_1, S1.Pin_2, R1.Pin_0
  N4: Part1.D2, S2.Pin_1, S2.Pin_2, R2.Pin_0
  N5: Part1.D3_PWM, S4.Pin_3, S4.Pin_4, R4.Pin_0
  N6: Part1.D5_PWM, S3.Pin_3, S3.Pin_4, R3.Pin_0
  N7: Part1.D6_PWM, J1.pin2
  N8: Part1.3V3, S1.Pin_3, S1.Pin_4, S2.Pin_3, S2.Pin_4, S3.Pin_1, S3.Pin_2, S4.Pin_1, S4.Pin_2
